// Logisim project 16-bit-CPU.circ as structural Verilog: 31 circuits, main circuit main
module main (
  input  [7:0] INPR,
  output [15:0] out_2,
  output [15:0] out_3,
  output [15:0] out_4,
  output [15:0] out_5,
  output [15:0] out_6,
  output [15:0] out_7,
  output [15:0] out_8,
  output [15:0] out_9
);

  wire ac_control_1_clr, ac_control_1_inc, ac_control_1_ld, ADD, AND, ar_control_1_clr, ar_control_1_inc,
       ar_control_1_ld, CLK, CLK_out, COMP, DR, dr_control_1_inc, dr_control_1_ld, E, e_control_1_e_j,
       e_control_1_e_k, E_OUT, FGI, fgi_fgo_control_1_fgi_j, fgi_fgo_control_1_fgi_k,
       fgi_fgo_control_1_fgo_k, FGO, I, IEN, ien_control_1_ien_j, ien_control_1_ien_k, INPR_t,
       memory_control_1_ld, not_1_out, not_2_out, outr_control_1_ld, pc_control_1_clr, pc_control_1_inc,
       pc_control_1_ld, R, r_control_1_r_j, r_control_1_r_k, S, sc_control_1_clr, SHL, SHR, tr_control_1_ld;
  wire [2:0] select;
  wire [3:0] outr_1_out, outr_1_out_2;
  wire [7:0] D;
  wire [11:0] B;
  wire [15:0] alu_16_bit_1_alu_out, T;

  FGI fgi_1 (.FGI_J(fgi_fgo_control_1_fgi_j), .CLK(CLK), .FGI_K(fgi_fgo_control_1_fgi_k), .FGI(FGI));
  IEN ien_1 (.IEN_J(ien_control_1_ien_j), .IEN_K(ien_control_1_ien_k), .CLK(CLK), .IEN(IEN));
  Clock u_CLK (.out(CLK_out));
  not not_1 (not_1_out, S);
  FGI___FGO_Control fgi_fgo_control_1 (
    .INPR(INPR), .I(I), .T(T), .D(D), .B(B), .FGI_J(fgi_fgo_control_1_fgi_j),
    .FGI_K(fgi_fgo_control_1_fgi_k), .FGO_K(fgi_fgo_control_1_fgo_k));
  IEN_Control ien_control_1 (
    .I(I), .T(T), .R(R), .D(D), .B(B), .IEN_J(ien_control_1_ien_j), .IEN_K(ien_control_1_ien_k));
  S s_1 (.CLK(CLK), .I(I), .T(T), .D(D), .B(B), .S(S));
  and and_1 (CLK, CLK_out, not_1_out);
  BUS_Selector_Encoder bus_selector_encoder_1 (.T(T), .D(D), .B(B), .R(R), .I(I), .select(select));
  FGO fgo_1 (.CLK(CLK), .FGO_K(fgi_fgo_control_1_fgo_k), .FGO(FGO));
  E e_1 (.E_j(e_control_1_e_j), .CLK(CLK), .E_k(e_control_1_e_k), .E(E));
  R r_1 (.R_J(r_control_1_r_j), .R_K(r_control_1_r_k), .CLK(CLK), .R(R));
  E_Control e_control_1 (.I(I), .T(T), .E_out(E_OUT), .D(D), .B(B), .E_j(e_control_1_e_j), .E_k(e_control_1_e_k));
  R_Control r_control_1 (.IEN(IEN), .FGI(FGI), .FGO(FGO), .T(T), .R(R), .R_J(r_control_1_r_j), .R_K(r_control_1_r_k));
  SC sc_1 (.CLR(sc_control_1_clr), .CLK(CLK), .out_3(T));
  SC_Control sc_control_1 (.R(R), .T(T), .D(D), .I(I), .CLR(sc_control_1_clr));
  Hex_Digit_Display hex_digit_display_1 (.value(out_9[11:8]));  // open: dp
  Hex_Digit_Display hex_digit_display_2 (.value(out_9[15:12]));  // open: dp
  Hex_Digit_Display hex_digit_display_3 (.value(out_9[3:0]));  // open: dp
  Hex_Digit_Display hex_digit_display_4 (.value(out_9[7:4]));  // open: dp
  Memory_Control memory_control_1 (.R(R), .T(T), .D(D), .LD(memory_control_1_ld));
  AR ar_1 (
    .LD(ar_control_1_ld), .INC(ar_control_1_inc), .CLK(CLK), .CLR(ar_control_1_clr), .Bus_out(out_3),
    .Bus_in(out_9));
  PC pc_1 (
    .LD(pc_control_1_ld), .INC(pc_control_1_inc), .CLK(CLK), .CLR(pc_control_1_clr), .Bus_out(out_4),
    .Bus_in(out_9));
  DR dr_1 (.LD(dr_control_1_ld), .Bus_in(out_9), .INC(dr_control_1_inc), .CLK(CLK), .Bus_out(out_5));
  DR_Control dr_control_1 (.T(T), .D(D), .LD(dr_control_1_ld), .INC(dr_control_1_inc));
  IR ir_1 (.T(T), .Buss_in(out_9), .R(R), .CLK(CLK), .B(B), .D(D), .I(I), .Bus_out(out_7));
  TR tr_1 (.LD(tr_control_1_ld), .Bus_in(out_9), .CLK(CLK), .Bus_out(out_8));
  TR_Control tr_control_1 (.R(R), .T(T), .LD(tr_control_1_ld));
  OUTR outr_1 (.LD(outr_control_1_ld), .CLK(CLK), .Bus_in(out_9), .OUT({outr_1_out_2, outr_1_out}));
  OUTR_Control outr_control_1 (.I(I), .T(T), .D(D), .B(B), .LD(outr_control_1_ld));
  RAM #(.addrWidth(12), .dataWidth(16), .bus("separate")) ram_1 (
    .addr(out_3[11:0]), .din(out_9), .data(out_2), .str(memory_control_1_ld), .clk(CLK), .ld(not_2_out));  // open: sel, clr
  not not_2 (not_2_out, memory_control_1_ld);
  AR_Control ar_control_1 (
    .R(I), .T(T), .I(R), .D(D), .CLR(ar_control_1_clr), .LD(ar_control_1_ld), .INC(ar_control_1_inc));
  PC_Control pc_control_1 (
    .R(R), .T(T), .DR(out_6), .D(D), .I(I), .B(B), .E(E), .AC(out_5), .FGI(FGI), .FGO(FGO),
    .CLR(pc_control_1_clr), .INC(pc_control_1_inc), .LD(pc_control_1_ld));
  ALU__16_bit alu_16_bit_1 (
    .AND(AND), .ADD(ADD), .DR(DR), .INPR(INPR_t), .COM(COMP), .SHR(SHR), .SHL(SHL), .E(E), .AC(out_6),
    .DR_2(out_5), .INPR_2(INPR), .ALU_out(alu_16_bit_1_alu_out), .E_out(E_OUT));
  AC ac_1 (
    .LD(ac_control_1_ld), .Bus_in(alu_16_bit_1_alu_out), .INC(ac_control_1_inc), .CLK(CLK),
    .CLR(ac_control_1_clr), .Bus_out(out_6));
  AC_Control ac_control_1 (
    .I(I), .T(T), .D(D), .B(B), .AND(AND), .ADD(ADD), .DR(DR), .SHL(SHL), .LD(ac_control_1_ld), .SHR(SHR),
    .COMP(COMP), .INPR(INPR_t), .CLR(ac_control_1_clr), .INC(ac_control_1_inc));
  Hex_Digit_Display hex_digit_display_5 (.value(out_2[15:12]));  // open: dp
  Hex_Digit_Display hex_digit_display_6 (.value(out_2[11:8]));  // open: dp
  Hex_Digit_Display hex_digit_display_7 (.value(out_2[7:4]));  // open: dp
  Hex_Digit_Display hex_digit_display_8 (.value(out_2[3:0]));  // open: dp
  Multiplexer #(.select(3), .width(16), .enable("false")) multiplexer_1 (
    .in1(out_3), .in2(out_4), .in3(out_5), .in4(out_6), .in5(out_7), .in6(out_8), .in7(out_2), .out(out_9),
    .sel(select));  // open: in0
  Hex_Digit_Display hex_digit_display_9 (.value(out_3[15:12]));  // open: dp
  Hex_Digit_Display hex_digit_display_10 (.value(out_3[11:8]));  // open: dp
  Hex_Digit_Display hex_digit_display_11 (.value(out_4[15:12]));  // open: dp
  Hex_Digit_Display hex_digit_display_12 (.value(out_4[11:8]));  // open: dp
  Hex_Digit_Display hex_digit_display_13 (.value(out_5[11:8]));  // open: dp
  Hex_Digit_Display hex_digit_display_14 (.value(out_5[15:12]));  // open: dp
  Hex_Digit_Display hex_digit_display_15 (.value(out_6[15:12]));  // open: dp
  Hex_Digit_Display hex_digit_display_16 (.value(out_6[11:8]));  // open: dp
  Hex_Digit_Display hex_digit_display_17 (.value(out_7[11:8]));  // open: dp
  Hex_Digit_Display hex_digit_display_18 (.value(out_7[15:12]));  // open: dp
  Hex_Digit_Display hex_digit_display_19 (.value(out_8[11:8]));  // open: dp
  Hex_Digit_Display hex_digit_display_20 (.value(out_8[15:12]));  // open: dp
  Hex_Digit_Display hex_digit_display_21 (.value(outr_1_out_2));  // open: dp
  Hex_Digit_Display hex_digit_display_22 (.value(outr_1_out));  // open: dp
  Hex_Digit_Display hex_digit_display_23 (.value(out_3[7:4]));  // open: dp
  Hex_Digit_Display hex_digit_display_24 (.value(out_3[3:0]));  // open: dp
  Hex_Digit_Display hex_digit_display_25 (.value(out_4[3:0]));  // open: dp
  Hex_Digit_Display hex_digit_display_26 (.value(out_4[7:4]));  // open: dp
  Hex_Digit_Display hex_digit_display_27 (.value(out_5[3:0]));  // open: dp
  Hex_Digit_Display hex_digit_display_28 (.value(out_5[7:4]));  // open: dp
  Hex_Digit_Display hex_digit_display_29 (.value(out_6[3:0]));  // open: dp
  Hex_Digit_Display hex_digit_display_30 (.value(out_6[7:4]));  // open: dp
  Hex_Digit_Display hex_digit_display_31 (.value(out_7[7:4]));  // open: dp
  Hex_Digit_Display hex_digit_display_32 (.value(out_7[3:0]));  // open: dp
  Hex_Digit_Display hex_digit_display_33 (.value(out_8[7:4]));  // open: dp
  Hex_Digit_Display hex_digit_display_34 (.value(out_8[3:0]));  // open: dp

  // Other names for the same wires on the sheet: AC_16[15:0] = out_6; DR_16[15:0] = out_5; INPR_8[7:0] = INPR

  // Notes on the sheet:
  //   Hossein Zandinejad
  //   610398129
  //   Final Project
endmodule

// FA
module Full_Adder (
  input  Ai,
  input  Bi,
  input  Ci,
  output Di,
  output Ci_1
);

  wire and_1_out, and_2_out, xor_1_out;

  xor xor_1 (xor_1_out, Ai, Bi);
  and and_1 (and_1_out, Bi, Ai);
  xor xor_2 (Di, xor_1_out, Ci);
  and and_2 (and_2_out, xor_1_out, Ci);
  or or_1 (Ci_1, and_2_out, and_1_out);

  // Notes on the sheet:
  //   Full Adder
endmodule

module AR (
  input  LD,
  input  INC,
  input  CLK,
  input  CLR,
  input  [15:0] Bus_in,
  output [15:0] Bus_out
);

  Counter #(.width(12), .max('hfff)) AR (
    .load(LD), .D(Bus_in[11:0]), .count(INC), .Q(Bus_out[11:0]), .clk(CLK), .clr(CLR));  // open: carry

  assign Bus_out[15:12] = 4'b0000;

  // Notes on the sheet:
  //   AR
endmodule

module AR_Control (
  input  R,
  input  [15:0] T,
  input  I,
  input  [7:0] D,
  output CLR,
  output LD,
  output INC
);

  wire and_2_out, and_3_out, and_4_out, not_1_out, not_2_out;

  not not_1 (not_1_out, R);
  not not_2 (not_2_out, D[7]);
  and and_1 (CLR, T[0], R);
  and and_2 (and_2_out, T[0], not_1_out);
  and and_3 (and_3_out, not_1_out, T[2]);
  and and_4 (and_4_out, not_2_out, I, T[3]);
  and and_5 (INC, D[5], T[4]);
  or or_1 (LD, and_2_out, and_3_out, and_4_out);

  // Notes on the sheet:
  //   AR Control
endmodule

module PC (
  input  LD,
  input  INC,
  input  CLK,
  input  CLR,
  input  [15:0] Bus_in,
  output [15:0] Bus_out
);

  Counter #(.width(12), .max('hfff)) PC (
    .load(LD), .D(Bus_in[11:0]), .count(INC), .Q(Bus_out[11:0]), .clk(CLK), .clr(CLR));  // open: carry

  assign Bus_out[15:12] = 4'b0000;

  // Notes on the sheet:
  //   PC
endmodule

module PC_Control (
  input  R,
  input  [15:0] T,
  input  [15:0] DR,
  input  [7:0] D,
  input  I,
  input  [11:0] B,
  input  E,
  input  [15:0] AC,
  input  FGI,
  input  FGO,
  output CLR,
  output INC,
  output LD
);

  wire AC_all, and_2_out, and_3_out, and_4_out, and_5_out, and_6_out, and_7_out, and_8_out, and_9_out,
       and_10_out, and_11_out, and_12_out, and_13_out, and_14_out, DR_all, not_1_out, not_2_out, not_3_out,
       not_4_out, not_5_out, not_6_out;

  not not_1 (not_1_out, DR_all);
  not not_2 (not_2_out, I);
  and and_1 (CLR, R, T[1]);
  not not_3 (not_3_out, R);
  and and_2 (and_2_out, not_3_out, T[1]);
  and and_3 (and_3_out, R, T[2]);
  and and_4 (and_4_out, D[6], T[6]);
  and and_5 (and_5_out, not_2_out, D[7], T[3]);
  and and_6 (and_6_out, T[3], D[7], I);
  and and_7 (and_7_out, D[4], T[4]);
  or or_1 (LD, and_7_out, and_8_out);
  and and_8 (and_8_out, D[5], T[5]);
  not not_4 (not_4_out, AC[15]);
  not not_5 (not_5_out, AC_all);
  not not_6 (not_6_out, E);
  and and_9 (and_9_out, B[4], and_5_out, not_4_out);
  and and_10 (and_10_out, AC[15], and_5_out, B[3]);
  and and_11 (and_11_out, not_5_out, and_5_out, B[2]);
  and and_12 (and_12_out, not_6_out, and_5_out, B[1]);
  and and_13 (and_13_out, FGI, and_6_out, B[9]);
  and and_14 (and_14_out, FGO, and_6_out, B[8]);
  or or_2 (INC, and_2_out, and_3_out, and_4_out, and_9_out, and_10_out, and_11_out, and_12_out, and_13_out, and_14_out);
  or or_3 (DR_all, DR[0], DR[1], DR[2], DR[3], DR[4], DR[5], DR[6], DR[7], DR[8], DR[9], DR[10], DR[11], DR[12], DR[13], DR[14], DR[15]);
  or or_4 (AC_all, AC[0], AC[1], AC[2], AC[3], AC[4], AC[5], AC[6], AC[7], AC[8], AC[9], AC[10], AC[11], AC[12], AC[13], AC[14], AC[15]);

  // Notes on the sheet:
  //   r
  //   p
  //   PC Control
endmodule

module DR (
  input  LD,
  input  [15:0] Bus_in,
  input  INC,
  input  CLK,
  output [15:0] Bus_out
);

  Counter #(.width(16), .max('hffff)) DR (
    .load(LD), .D(Bus_in), .count(INC), .Q(Bus_out), .clk(CLK));  // open: carry, clr

  // Notes on the sheet:
  //   DR
endmodule

module DR_Control (
  input  [15:0] T,
  input  [7:0] D,
  output LD,
  output INC
);

  wire and_1_out, and_2_out, and_3_out, and_4_out;

  and and_1 (and_1_out, T[4], D[0]);
  and and_2 (and_2_out, D[1], T[4]);
  and and_3 (and_3_out, D[2], T[4]);
  and and_4 (and_4_out, D[6], T[4]);
  and and_5 (INC, D[6], T[5]);
  or or_1 (LD, and_1_out, and_2_out, and_3_out, and_4_out);

  // Notes on the sheet:
  //   DR Control
endmodule

module AC (
  input  LD,
  input  [15:0] Bus_in,
  input  INC,
  input  CLK,
  input  CLR,
  output [15:0] Bus_out
);

  Counter #(.width(16), .max('hffff)) AC (
    .load(LD), .D(Bus_in), .count(INC), .Q(Bus_out), .clk(CLK), .clr(CLR));  // open: carry

  // Notes on the sheet:
  //   AC
endmodule

module AC_Control (
  input  I,
  input  [15:0] T,
  input  [7:0] D,
  input  [11:0] B,
  output AND,
  output ADD,
  output DR,
  output SHL,
  output LD,
  output SHR,
  output COMP,
  output INPR,
  output CLR,
  output INC
);

  wire not_1_out, p, r;

  not not_1 (not_1_out, I);
  and and_1 (r, not_1_out, D[7], T[3]);
  and and_2 (p, D[7], D[7], I);
  and and_3 (AND, T[5], D[0]);
  and and_4 (ADD, D[1], T[5]);
  and and_5 (DR, D[2], T[5]);
  and and_6 (SHL, r, B[6]);
  and and_7 (SHR, B[7], r);
  and and_8 (COMP, B[9], r);
  and and_9 (INPR, B[11], p);
  and and_10 (CLR, r, B[11]);
  and and_11 (INC, r, B[5]);
  or or_1 (LD, AND, ADD, DR, SHL, SHR, COMP, INPR);

  // Notes on the sheet:
  //   AC Control
endmodule

module TR (
  input  LD,
  input  [15:0] Bus_in,
  input  CLK,
  output [15:0] Bus_out
);

  Counter #(.width(16), .max('hffff)) TR (
    .load(LD), .D(Bus_in), .count(1'b0), .Q(Bus_out), .clk(CLK));  // open: carry, clr

  // Notes on the sheet:
  //   TR
endmodule

module TR_Control (
  input  R,
  input  [15:0] T,
  output LD
);

  and and_1 (LD, R, T[0]);

  // Notes on the sheet:
  //   TR Control
endmodule

module OUTR (
  input  LD,
  input  CLK,
  input  [15:0] Bus_in,
  output [7:0] OUT
);

  Register OUTR (.D(Bus_in[7:0]), .en(LD), .Q(OUT), .clk(CLK));  // open: clr

  // Notes on the sheet:
  //   OUTR
endmodule

module OUTR_Control (
  input  I,
  input  [15:0] T,
  input  [7:0] D,
  input  [11:0] B,
  output LD
);

  wire and_1_out;

  and and_1 (and_1_out, I, D[7], T[3]);
  and and_2 (LD, and_1_out, B[10]);

  // Notes on the sheet:
  //   OUTR Control
endmodule

module SC (
  input  CLR,
  input  CLK,
  output [15:0] out_3
);

  wire not_1_out;
  wire [3:0] SC_q;

  not not_1 (not_1_out, CLR);
  Counter #(.width(4), .max('hf)) SC (
    .load(CLR), .D(4'b0000), .count(not_1_out), .Q(SC_q), .clk(CLK));  // open: carry, clr
  Decoder #(.select(4), .enable("false")) decoder_1 (
    .out0(out_3[0]), .out1(out_3[1]), .out2(out_3[2]), .out3(out_3[3]), .out4(out_3[4]), .out5(out_3[5]),
    .out6(out_3[6]), .out7(out_3[7]), .out8(out_3[8]), .out9(out_3[9]), .out10(out_3[10]), .out11(out_3[11]),
    .out12(out_3[12]), .out13(out_3[13]), .out14(out_3[14]), .out15(out_3[15]), .sel(SC_q));

  // Notes on the sheet:
  //   SC
endmodule

module SC_Control (
  input  R,
  input  [15:0] T,
  input  [7:0] D,
  input  I,
  output CLR
);

  wire and_1_out, and_2_out, and_3_out, and_4_out, and_5_out, and_6_out, and_7_out, and_8_out, and_9_out,
       and_10_out, not_1_out;

  not not_1 (not_1_out, I);
  and and_1 (and_1_out, R, T[2]);
  and and_2 (and_2_out, T[5], D[0]);
  and and_3 (and_3_out, D[1], T[5]);
  and and_4 (and_4_out, D[2], T[5]);
  and and_5 (and_5_out, D[5], T[5]);
  and and_6 (and_6_out, T[4], D[3]);
  and and_7 (and_7_out, D[4], T[4]);
  and and_8 (and_8_out, T[6], D[6]);
  and and_9 (and_9_out, not_1_out, D[7], T[3]);
  and and_10 (and_10_out, D[7], D[7], I);
  or or_1 (CLR, and_1_out, and_2_out, and_3_out, and_4_out, and_5_out, and_6_out, and_7_out, and_8_out, and_9_out, and_10_out);

  // Notes on the sheet:
  //   SC Control
endmodule

module IEN (
  input  IEN_J,
  input  IEN_K,
  input  CLK,
  output IEN
);

  J_K_Flip_Flop u_IEN (.J(IEN_J), .clk(CLK), .K(IEN_K), .Q(IEN));  // open: Qn, preset, en, reset

  // Notes on the sheet:
  //   IEN
endmodule

module IEN_Control (
  input  I,
  input  [15:0] T,
  input  R,
  input  [7:0] D,
  input  [11:0] B,
  output IEN_J,
  output IEN_K
);

  wire and_2_out, and_3_out, P;

  and u_P (P, I, D[7], T[3]);
  and and_1 (IEN_J, B[7], P);
  and and_2 (and_2_out, P, B[6]);
  and and_3 (and_3_out, R, T[2]);
  or or_1 (IEN_K, and_2_out, and_3_out);

  // Notes on the sheet:
  //   IEN Control
endmodule

module FGI (
  input  FGI_J,
  input  CLK,
  input  FGI_K,
  output FGI
);

  J_K_Flip_Flop u_FGI (.J(FGI_J), .clk(CLK), .K(FGI_K), .Q(FGI));  // open: Qn, preset, en, reset

  // Notes on the sheet:
  //   FGI
endmodule

module FGO (
  input  CLK,
  input  FGO_K,
  output FGO
);

  J_K_Flip_Flop u_FGO (.J(1'b0), .clk(CLK), .K(FGO_K), .Q(FGO));  // open: Qn, preset, en, reset

  // Notes on the sheet:
  //   FGO
endmodule

module FGI___FGO_Control (
  input  [7:0] INPR,
  input  I,
  input  [15:0] T,
  input  [7:0] D,
  input  [11:0] B,
  output FGI_J,
  output FGI_K,
  output FGO_K
);

  wire p;

  or or_1 (FGI_J, INPR[0], INPR[1], INPR[2], INPR[3], INPR[4], INPR[5], INPR[6], INPR[7]);
  and and_1 (p, I, D[7], T[3]);
  and and_2 (FGI_K, p, B[11]);
  and and_3 (FGO_K, p, B[10]);

  // Notes on the sheet:
  //   FGI and FGO  Control
endmodule

module S (
  input  CLK,
  input  I,
  input  [15:0] T,
  input  [7:0] D,
  input  [11:0] B,
  output S
);

  wire and_1_out, and_2_out, not_1_out;

  not not_1 (not_1_out, I);
  and and_1 (and_1_out, not_1_out, D[7], T[3]);
  and and_2 (and_2_out, and_1_out, B[0]);
  J_K_Flip_Flop u_S (.J(and_2_out), .clk(CLK), .K(1'b0), .Q(S));  // open: Qn, preset, en, reset

  // Notes on the sheet:
  //   Flip-Flop S
  //   r
endmodule

module E (
  input  E_j,
  input  CLK,
  input  E_k,
  output E
);

  J_K_Flip_Flop u_E (.J(E_j), .clk(CLK), .K(E_k), .Q(E));  // open: Qn, preset, en, reset

  // Notes on the sheet:
  //   Flip-Flop E
endmodule

module E_Control (
  input  I,
  input  [15:0] T,
  input  E_out,
  input  [7:0] D,
  input  [11:0] B,
  output E_j,
  output E_k
);

  wire and_2_out, and_3_out, and_4_out, and_5_out, not_1_out, not_2_out, not_3_out, or_1_out, r;

  not not_1 (not_1_out, I);
  and and_1 (r, not_1_out, D[7], T[3]);
  and and_2 (and_2_out, r, B[8]);
  or or_1 (or_1_out, and_2_out, and_3_out);
  and and_3 (and_3_out, r, B[10]);
  not not_2 (not_2_out, or_1_out);
  not not_3 (not_3_out, E_out);
  and and_4 (and_4_out, not_2_out, E_out);
  and and_5 (and_5_out, not_2_out, not_3_out);
  or or_2 (E_j, and_2_out, and_4_out);
  or or_3 (E_k, and_5_out, and_2_out, and_3_out);

  // Notes on the sheet:
  //   E Control
endmodule

module R (
  input  R_J,
  input  R_K,
  input  CLK,
  output R
);

  J_K_Flip_Flop u_R (.J(R_J), .clk(CLK), .K(R_K), .Q(R));  // open: Qn, preset, en, reset

  // Notes on the sheet:
  //   Flip-Flop R
endmodule

module R_Control (
  input  IEN,
  input  FGI,
  input  FGO,
  input  [15:0] T,
  input  R,
  output R_J,
  output R_K
);

  wire not_1_out, not_2_out, not_3_out, or_1_out;

  not not_1 (not_1_out, T[0]);
  not not_2 (not_2_out, T[1]);
  or or_1 (or_1_out, FGI, FGO);
  not not_3 (not_3_out, T[2]);
  and and_1 (R_K, T[2], R);
  and and_2 (R_J, not_1_out, not_2_out, IEN, or_1_out, not_3_out);

  // Notes on the sheet:
  //   R Control
endmodule

module IR (
  input  [15:0] T,
  input  [15:0] Buss_in,
  input  R,
  input  CLK,
  output [11:0] B,
  output [15:0] Bus_out,
  output [7:0] D,
  output I
);

  wire and_1_out, and_2_out, not_1_out;

  not not_1 (not_1_out, R);
  and and_1 (and_1_out, not_1_out, T[1]);
  and and_2 (and_2_out, not_1_out, T[2]);
  Register #(.width(16)) IR (.D(Buss_in), .en(and_1_out), .Q({Bus_out[15:12], B}), .clk(CLK));  // open: clr
  D_Flip_Flop u_I (.clk(CLK), .D(Bus_out[15]), .Q(I), .en(and_2_out));  // open: Qn, preset, reset
  Decoder #(.select(3), .enable("false")) decoder_1 (
    .out0(D[0]), .out1(D[1]), .out2(D[2]), .out3(D[3]), .out4(D[4]), .out5(D[5]), .out6(D[6]), .out7(D[7]),
    .sel(Bus_out[14:12]));

  assign Bus_out[11:0] = B;

  // Notes on the sheet:
  //   IR
endmodule

module BUS_Selector_Encoder (
  input  [15:0] T,
  input  [7:0] D,
  input  [11:0] B,
  input  R,
  input  I,
  output [2:0] select
);

  wire and_3_out, and_4_out, and_5_out, and_6_out, and_7_out, and_8_out, and_9_out, and_10_out, and_11_out,
       and_12_out, and_13_out, and_14_out, and_15_out, and_16_out, and_17_out, and_18_out, not_1_out,
       not_2_out, not_3_out, or_1_out, or_2_out, or_3_out, or_4_out, or_5_out, P, r_t;

  not not_1 (not_1_out, D[7]);
  and and_1 (P, D[7], I, T[3]);
  and and_2 (r_t, not_1_out, I, T[3]);
  not not_2 (not_2_out, R);
  not not_3 (not_3_out, R);
  and and_3 (and_3_out, D[4], T[4]);
  and and_4 (and_4_out, D[5], T[5]);
  and and_5 (and_5_out, D[5], T[4]);
  and and_6 (and_6_out, R, T[0]);
  and and_7 (and_7_out, not_2_out, T[0]);
  and and_8 (and_8_out, D[2], T[5]);
  and and_9 (and_9_out, D[6], T[6]);
  and and_10 (and_10_out, D[3], T[4]);
  and and_11 (and_11_out, P, B[10]);
  and and_12 (and_12_out, T[2], not_3_out);
  and and_13 (and_13_out, R, T[1]);
  and and_14 (and_14_out, T[4], D[0]);
  and and_15 (and_15_out, T[4], D[1]);
  and and_16 (and_16_out, T[4], D[2]);
  and and_17 (and_17_out, T[4], D[6]);
  and and_18 (and_18_out, ~R, T[1]);  // AND_Gate
  or or_1 (or_1_out, and_3_out, and_4_out);
  or or_2 (or_2_out, and_5_out, and_6_out, and_7_out);
  or or_3 (or_3_out, and_8_out, and_9_out);
  or or_4 (or_4_out, and_10_out, and_11_out);
  or or_5 (or_5_out, and_14_out, and_15_out, and_16_out, and_17_out, and_18_out, r_t);
  Priority_Encoder priority_encoder_1 (
    .in1(or_1_out), .in2(or_2_out), .in3(or_3_out), .in4(or_4_out), .in5(and_12_out), .in6(and_13_out),
    .in7(or_5_out), .out(select));  // open: in0, en_in, gs, en_out

  // Notes on the sheet:
  //   BUS Selector Encoder
endmodule

module Memory_Control (
  input  R,
  input  [15:0] T,
  input  [7:0] D,
  output LD
);

  wire and_1_out, and_2_out, and_3_out, and_4_out;

  and and_1 (and_1_out, R, T[1]);
  and and_2 (and_2_out, D[3], T[4]);
  and and_3 (and_3_out, T[4], D[5]);
  and and_4 (and_4_out, D[6], T[6]);
  or or_1 (LD, and_1_out, and_2_out, and_3_out, and_4_out);

  // Notes on the sheet:
  //   Memory Control
endmodule

module ALU__1_Bit (
  input  DR_i,
  input  AC_i,
  input  AND,
  input  C_i,
  input  ADD,
  input  DR,
  input  INPR_i,
  input  INPR,
  input  COM,
  input  SHR,
  input  AC_i_1,
  input  SHL,
  input  AC_i_1_2,
  output C_i_1,
  output ALU_OUT
);

  wire ADD_out, AND_out, COM_out, DR_out, full_adder_1_di, INPR_out, not_1_out, SHL_out, SHR_out;

  Full_Adder full_adder_1 (.Ai(AC_i), .Bi(DR_i), .Ci(C_i), .Di(full_adder_1_di), .Ci_1(C_i_1));
  not not_1 (not_1_out, AC_i);
  and u_AND (AND_out, DR_i, AC_i, AND);
  and u_ADD (ADD_out, full_adder_1_di, ADD);
  and u_DR (DR_out, DR_i, DR);
  and u_INPR (INPR_out, INPR_i, INPR);
  and u_COM (COM_out, not_1_out, COM);
  and u_SHR (SHR_out, SHR, AC_i_1);
  and u_SHL (SHL_out, SHL, AC_i_1_2);
  or or_1 (ALU_OUT, AND_out, ADD_out, DR_out, INPR_out, COM_out, SHR_out, SHL_out);

  // Notes on the sheet:
  //   ALU (1 Bit)
endmodule

module ALU__16_bit (
  input  AND,
  input  ADD,
  input  DR,
  input  INPR,
  input  COM,
  input  SHR,
  input  SHL,
  input  E,
  input  [15:0] AC,
  input  [15:0] DR_2,
  input  [7:0] INPR_2,
  output E_out,
  output [15:0] ALU_out
);

  wire alu_1_bit_1_c_i_1, alu_1_bit_2_c_i_1, alu_1_bit_3_c_i_1, alu_1_bit_4_c_i_1, alu_1_bit_5_c_i_1,
       alu_1_bit_6_c_i_1, alu_1_bit_7_c_i_1, alu_1_bit_8_c_i_1, alu_1_bit_9_c_i_1, alu_1_bit_10_c_i_1,
       alu_1_bit_11_c_i_1, alu_1_bit_12_c_i_1, alu_1_bit_13_c_i_1, alu_1_bit_14_c_i_1, alu_1_bit_15_c_i_1,
       and_1_out, and_2_out, and_3_out, and_4_out, COUT, not_1_out, or_1_out;

  ALU__1_Bit alu_1_bit_1 (
    .DR_i(DR_2[0]), .AC_i(AC[0]), .AND(AND), .C_i(1'b0), .ADD(ADD), .DR(DR), .INPR_i(INPR_2[0]), .INPR(INPR),
    .COM(COM), .SHR(SHR), .AC_i_1(AC[1]), .SHL(SHL), .AC_i_1_2(E), .C_i_1(alu_1_bit_1_c_i_1),
    .ALU_OUT(ALU_out[0]));
  ALU__1_Bit alu_1_bit_2 (
    .DR_i(DR_2[8]), .AC_i(AC[8]), .AND(AND), .C_i(alu_1_bit_15_c_i_1), .ADD(ADD), .DR(DR), .INPR_i(1'b0),
    .INPR(INPR), .COM(COM), .SHR(SHR), .AC_i_1(AC[9]), .SHL(SHL), .AC_i_1_2(AC[7]),
    .C_i_1(alu_1_bit_2_c_i_1), .ALU_OUT(ALU_out[8]));
  ALU__1_Bit alu_1_bit_3 (
    .DR_i(DR_2[1]), .AC_i(AC[1]), .AND(AND), .C_i(alu_1_bit_1_c_i_1), .ADD(ADD), .DR(DR), .INPR_i(INPR_2[1]),
    .INPR(INPR), .COM(COM), .SHR(SHR), .AC_i_1(AC[2]), .SHL(SHL), .AC_i_1_2(AC[0]),
    .C_i_1(alu_1_bit_3_c_i_1), .ALU_OUT(ALU_out[1]));
  ALU__1_Bit alu_1_bit_4 (
    .DR_i(DR_2[9]), .AC_i(AC[9]), .AND(AND), .C_i(alu_1_bit_2_c_i_1), .ADD(ADD), .DR(DR), .INPR_i(1'b0),
    .INPR(INPR), .COM(COM), .SHR(SHR), .AC_i_1(AC[10]), .SHL(SHL), .AC_i_1_2(AC[8]),
    .C_i_1(alu_1_bit_4_c_i_1), .ALU_OUT(ALU_out[9]));
  ALU__1_Bit alu_1_bit_5 (
    .DR_i(DR_2[2]), .AC_i(AC[2]), .AND(AND), .C_i(alu_1_bit_3_c_i_1), .ADD(ADD), .DR(DR), .INPR_i(INPR_2[2]),
    .INPR(INPR), .COM(COM), .SHR(SHR), .AC_i_1(AC[3]), .SHL(SHL), .AC_i_1_2(AC[1]),
    .C_i_1(alu_1_bit_5_c_i_1), .ALU_OUT(ALU_out[2]));
  ALU__1_Bit alu_1_bit_6 (
    .DR_i(DR_2[10]), .AC_i(AC[10]), .AND(AND), .C_i(alu_1_bit_4_c_i_1), .ADD(ADD), .DR(DR), .INPR_i(1'b0),
    .INPR(INPR), .COM(COM), .SHR(SHR), .AC_i_1(AC[11]), .SHL(SHL), .AC_i_1_2(AC[9]),
    .C_i_1(alu_1_bit_6_c_i_1), .ALU_OUT(ALU_out[10]));
  ALU__1_Bit alu_1_bit_7 (
    .DR_i(DR_2[3]), .AC_i(AC[3]), .AND(AND), .C_i(alu_1_bit_5_c_i_1), .ADD(ADD), .DR(DR), .INPR_i(INPR_2[3]),
    .INPR(INPR), .COM(COM), .SHR(SHR), .AC_i_1(AC[4]), .SHL(SHL), .AC_i_1_2(AC[2]),
    .C_i_1(alu_1_bit_7_c_i_1), .ALU_OUT(ALU_out[3]));
  ALU__1_Bit alu_1_bit_8 (
    .DR_i(DR_2[11]), .AC_i(AC[11]), .AND(AND), .C_i(alu_1_bit_6_c_i_1), .ADD(ADD), .DR(DR), .INPR_i(1'b0),
    .INPR(INPR), .COM(COM), .SHR(SHR), .AC_i_1(AC[12]), .SHL(SHL), .AC_i_1_2(AC[10]),
    .C_i_1(alu_1_bit_8_c_i_1), .ALU_OUT(ALU_out[11]));
  ALU__1_Bit alu_1_bit_9 (
    .DR_i(DR_2[4]), .AC_i(AC[4]), .AND(AND), .C_i(alu_1_bit_7_c_i_1), .ADD(ADD), .DR(DR), .INPR_i(INPR_2[4]),
    .INPR(INPR), .COM(COM), .SHR(SHR), .AC_i_1(AC[5]), .SHL(SHL), .AC_i_1_2(AC[3]),
    .C_i_1(alu_1_bit_9_c_i_1), .ALU_OUT(ALU_out[4]));
  ALU__1_Bit alu_1_bit_10 (
    .DR_i(DR_2[12]), .AC_i(AC[12]), .AND(AND), .C_i(alu_1_bit_8_c_i_1), .ADD(ADD), .DR(DR), .INPR_i(1'b0),
    .INPR(INPR), .COM(COM), .SHR(SHR), .AC_i_1(AC[13]), .SHL(SHL), .AC_i_1_2(AC[11]),
    .C_i_1(alu_1_bit_10_c_i_1), .ALU_OUT(ALU_out[12]));
  ALU__1_Bit alu_1_bit_11 (
    .DR_i(DR_2[5]), .AC_i(AC[5]), .AND(AND), .C_i(alu_1_bit_9_c_i_1), .ADD(ADD), .DR(DR), .INPR_i(INPR_2[5]),
    .INPR(INPR), .COM(COM), .SHR(SHR), .AC_i_1(AC[6]), .SHL(SHL), .AC_i_1_2(AC[4]),
    .C_i_1(alu_1_bit_11_c_i_1), .ALU_OUT(ALU_out[5]));
  ALU__1_Bit alu_1_bit_12 (
    .DR_i(DR_2[13]), .AC_i(AC[13]), .AND(AND), .C_i(alu_1_bit_10_c_i_1), .ADD(ADD), .DR(DR), .INPR_i(1'b0),
    .INPR(INPR), .COM(COM), .SHR(SHR), .AC_i_1(AC[14]), .SHL(SHL), .AC_i_1_2(AC[12]),
    .C_i_1(alu_1_bit_12_c_i_1), .ALU_OUT(ALU_out[13]));
  ALU__1_Bit alu_1_bit_13 (
    .DR_i(DR_2[6]), .AC_i(AC[6]), .AND(AND), .C_i(alu_1_bit_11_c_i_1), .ADD(ADD), .DR(DR),
    .INPR_i(INPR_2[6]), .INPR(INPR), .COM(COM), .SHR(SHR), .AC_i_1(AC[7]), .SHL(SHL), .AC_i_1_2(AC[5]),
    .C_i_1(alu_1_bit_13_c_i_1), .ALU_OUT(ALU_out[6]));
  ALU__1_Bit alu_1_bit_14 (
    .DR_i(DR_2[14]), .AC_i(AC[14]), .AND(AND), .C_i(alu_1_bit_12_c_i_1), .ADD(ADD), .DR(DR), .INPR_i(1'b0),
    .INPR(INPR), .COM(COM), .SHR(SHR), .AC_i_1(AC[15]), .SHL(SHL), .AC_i_1_2(AC[13]),
    .C_i_1(alu_1_bit_14_c_i_1), .ALU_OUT(ALU_out[14]));
  ALU__1_Bit alu_1_bit_15 (
    .DR_i(DR_2[7]), .AC_i(AC[7]), .AND(AND), .C_i(alu_1_bit_13_c_i_1), .ADD(ADD), .DR(DR),
    .INPR_i(INPR_2[7]), .INPR(INPR), .COM(COM), .SHR(SHR), .AC_i_1(AC[8]), .SHL(SHL), .AC_i_1_2(AC[6]),
    .C_i_1(alu_1_bit_15_c_i_1), .ALU_OUT(ALU_out[7]));
  ALU__1_Bit alu_1_bit_16 (
    .DR_i(DR_2[15]), .AC_i(AC[15]), .AND(AND), .C_i(alu_1_bit_14_c_i_1), .ADD(ADD), .DR(DR), .INPR_i(1'b0),
    .INPR(INPR), .COM(COM), .SHR(SHR), .AC_i_1(E), .SHL(SHL), .AC_i_1_2(AC[14]), .C_i_1(COUT),
    .ALU_OUT(ALU_out[15]));
  and and_1 (and_1_out, AC[15], SHL);
  and and_2 (and_2_out, COUT, ADD);
  and and_3 (and_3_out, AC[0], SHR);
  not not_1 (not_1_out, or_1_out);
  or or_1 (or_1_out, and_1_out, and_2_out, and_3_out);
  and and_4 (and_4_out, not_1_out, E);
  or or_2 (E_out, or_1_out, and_4_out);

  // Other names for the same wires on the sheet: ALU0 = ALU_out[0]; ALU1 = ALU_out[1]; ALU2 = ALU_out[2];
  //   ALU3 = ALU_out[3]; ALU4 = ALU_out[4]; ALU5 = ALU_out[5]; ALU6 = ALU_out[6]; ALU7 = ALU_out[7];
  //   ALU8 = ALU_out[8]; ALU9 = ALU_out[9]; ALU10 = ALU_out[10]; ALU11 = ALU_out[11]; ALU12 = ALU_out[12];
  //   ALU13 = ALU_out[13]; ALU14 = ALU_out[14]; ALU15 = ALU_out[15]; DR0 = DR_2[0]; DR1 = DR_2[1]; DR2 = DR_2[2];
  //   DR3 = DR_2[3]; DR4 = DR_2[4]; DR5 = DR_2[5]; DR6 = DR_2[6]; DR7 = DR_2[7]; DR8 = DR_2[8]; DR9 = DR_2[9];
  //   DR10 = DR_2[10]; DR11 = DR_2[11]; DR12 = DR_2[12]; DR13 = DR_2[13]; DR14 = DR_2[14]; DR15 = DR_2[15];
  //   INP0 = INPR_2[0]; INP1 = INPR_2[1]; INP2 = INPR_2[2]; INP3 = INPR_2[3]; INP4 = INPR_2[4]; INP5 = INPR_2[5];
  //   INP6 = INPR_2[6]; INP7 = INPR_2[7]

  // Notes on the sheet:
  //   ALU (16 Bit)
endmodule
